// Logisim project Arkanoid.circ as structural Verilog: 18 circuits, main circuit main
// Points
module main (
);

  wire clock_1_out, game_system__16_1_out_59, game_system__16_1_out_60, game_system__16_1_out_63,
       game_system__16_1_out_68, game_system__16_1_out_70, S_T_A_R_T_out;
  wire [3:0] game_system__16_1_out_64, game_system__16_1_out_65, game_system__16_1_out_66,
       game_system__16_1_out_67;
  wire [6:0] keyboard_1_data;
  wire [7:0] game_system__16_1_out_61, game_system__16_1_out_69;
  wire [8:0] game_system__16_1_out_17, game_system__16_1_out_18, game_system__16_1_out_19,
       game_system__16_1_out_20, game_system__16_1_out_21, game_system__16_1_out_22,
       game_system__16_1_out_23, game_system__16_1_out_24, game_system__16_1_out_25,
       game_system__16_1_out_26, game_system__16_1_out_27, game_system__16_1_out_28,
       game_system__16_1_out_29, game_system__16_1_out_30, game_system__16_1_out_31,
       game_system__16_1_out_32, game_system__16_1_out_33, game_system__16_1_out_34,
       game_system__16_1_out_35, game_system__16_1_out_36, game_system__16_1_out_39,
       game_system__16_1_out_40, game_system__16_1_out_43, game_system__16_1_out_46, game_system__16_1_out_49;
  wire [15:0] game_system__16_1_out_37, game_system__16_1_out_38, game_system__16_1_out_41,
       game_system__16_1_out_42, game_system__16_1_out_44, game_system__16_1_out_45,
       game_system__16_1_out_47, game_system__16_1_out_48, game_system__16_1_out_50,
       game_system__16_1_out_51, game_system__16_1_out_52, game_system__16_1_out_53,
       game_system__16_1_out_54, game_system__16_1_out_55, game_system__16_1_out_56,
       game_system__16_1_out_57, game_system__16_1_out_58, game_system__16_1_out_62;

  Keyboard #(.buflen(1)) keyboard_1 (.clk(clock_1_out), .data(keyboard_1_data));  // open: re, clr, avail
  Clock clock_1 (.out(clock_1_out));
  DotMatrix #(.inputtype("row"), .matrixcols(16), .matrixrows(1)) dotmatrix_1 (.row0(game_system__16_1_out_51));
  DotMatrix #(.inputtype("row"), .matrixcols(16), .matrixrows(16)) dotmatrix_2 (
    .row0(game_system__16_1_out_37), .row1(game_system__16_1_out_41), .row2(game_system__16_1_out_44),
    .row3(game_system__16_1_out_47), .row4(game_system__16_1_out_50), .row5(game_system__16_1_out_53),
    .row6(game_system__16_1_out_55), .row7(game_system__16_1_out_57), .row8(game_system__16_1_out_38),
    .row9(game_system__16_1_out_42), .row10(game_system__16_1_out_45), .row11(game_system__16_1_out_48),
    .row12(game_system__16_1_out_52), .row13(game_system__16_1_out_54), .row14(game_system__16_1_out_56),
    .row15(game_system__16_1_out_58));
  DotMatrix #(.matrixcols(27), .matrixrows(9)) dotmatrix_3 (
    .col1(game_system__16_1_out_17), .col2(game_system__16_1_out_18), .col3(game_system__16_1_out_19),
    .col4(game_system__16_1_out_20), .col5(game_system__16_1_out_21), .col6(game_system__16_1_out_22),
    .col7(game_system__16_1_out_23), .col8(game_system__16_1_out_24), .col9(game_system__16_1_out_25),
    .col10(game_system__16_1_out_27), .col11(game_system__16_1_out_29), .col12(game_system__16_1_out_31),
    .col13(game_system__16_1_out_33), .col14(game_system__16_1_out_35), .col15(game_system__16_1_out_39),
    .col16(game_system__16_1_out_43), .col17(game_system__16_1_out_46), .col18(game_system__16_1_out_49),
    .col19(game_system__16_1_out_26), .col20(game_system__16_1_out_28), .col21(game_system__16_1_out_30),
    .col22(game_system__16_1_out_32), .col23(game_system__16_1_out_34), .col24(game_system__16_1_out_36),
    .col25(game_system__16_1_out_40));  // open: col0, col26
  Button S_T_A_R_T (.out(S_T_A_R_T_out));
  Hex_Digit_Display hex_digit_display_1 (.value(game_system__16_1_out_69[7:4]));  // open: dp
  Hex_Digit_Display hex_digit_display_2 (.value(game_system__16_1_out_64));  // open: dp
  Hex_Digit_Display hex_digit_display_3 (.value(game_system__16_1_out_69[3:0]));  // open: dp
  Hex_Digit_Display hex_digit_display_4 (.value(game_system__16_1_out_65));  // open: dp
  GAME__SYSTEM__16 game_system__16_1 (
    .in_2(keyboard_1_data), .in_8(game_system__16_1_out_67), .in_13(game_system__16_1_out_61),
    .in_14(game_system__16_1_out_69), .in_15(game_system__16_1_out_60), .in_16(game_system__16_1_out_59),
    .out_51(game_system__16_1_out_51), .out_59(game_system__16_1_out_59), .out_60(game_system__16_1_out_60),
    .out_61(game_system__16_1_out_61), .in_12(S_T_A_R_T_out), .out_69(game_system__16_1_out_69),
    .out_70(game_system__16_1_out_70), .in_6(game_system__16_1_out_66), .in_4(game_system__16_1_out_62),
    .in_3(game_system__16_1_out_67), .in_7(game_system__16_1_out_68), .out_64(game_system__16_1_out_64),
    .out_65(game_system__16_1_out_65), .out_38(game_system__16_1_out_38), .out_42(game_system__16_1_out_42),
    .out_45(game_system__16_1_out_45), .out_48(game_system__16_1_out_48), .out_52(game_system__16_1_out_52),
    .out_54(game_system__16_1_out_54), .out_56(game_system__16_1_out_56), .out_58(game_system__16_1_out_58),
    .in_1(game_system__16_1_out_70), .out_57(game_system__16_1_out_57), .out_55(game_system__16_1_out_55),
    .out_53(game_system__16_1_out_53), .out_50(game_system__16_1_out_50), .out_47(game_system__16_1_out_47),
    .out_44(game_system__16_1_out_44), .out_41(game_system__16_1_out_41), .out_37(game_system__16_1_out_37),
    .out_17(game_system__16_1_out_17), .out_18(game_system__16_1_out_18), .out_19(game_system__16_1_out_19),
    .out_20(game_system__16_1_out_20), .out_21(game_system__16_1_out_21), .out_22(game_system__16_1_out_22),
    .out_23(game_system__16_1_out_23), .out_24(game_system__16_1_out_24), .out_25(game_system__16_1_out_25),
    .out_27(game_system__16_1_out_27), .out_29(game_system__16_1_out_29), .out_31(game_system__16_1_out_31),
    .out_33(game_system__16_1_out_33), .out_35(game_system__16_1_out_35), .out_39(game_system__16_1_out_39),
    .out_43(game_system__16_1_out_43), .out_46(game_system__16_1_out_46), .out_49(game_system__16_1_out_49),
    .out_26(game_system__16_1_out_26), .out_28(game_system__16_1_out_28), .out_30(game_system__16_1_out_30),
    .out_32(game_system__16_1_out_32), .out_34(game_system__16_1_out_34), .out_36(game_system__16_1_out_36),
    .out_40(game_system__16_1_out_40), .in_10(game_system__16_1_out_68), .in_11(game_system__16_1_out_63),
    .in_9(game_system__16_1_out_63), .in_5(game_system__16_1_out_63), .out_67(game_system__16_1_out_67),
    .out_66(game_system__16_1_out_66), .out_62(game_system__16_1_out_62), .out_68(game_system__16_1_out_68),
    .out_63(game_system__16_1_out_63));

  // Notes on the sheet:
  //   Zalecany tick-rate: 32
  //   Sterowanie:
  //   Platforma w lewo: klawisz a
  //   Platforma w prawo: klawisz d
  //   Uruchomienie gry - przycisk START
  //   Sterowanie platformą: KLAWIATURA
  //   Domyślny warunek wygranej: 7 punktów
  //   Restart gry: Wciśnięcie przycisku START
  //   Najwyższy zdobyty wynik
  //   Obecny wynik
endmodule

// #1
module BALL__SHIFTER__1 (
  input  [15:0] in_1,
  input  [3:0] INPUT,
  output [15:0] out_3
);

  wire multiplexer_1_out, multiplexer_2_out, multiplexer_3_out, multiplexer_4_out, multiplexer_5_out,
       multiplexer_6_out, multiplexer_7_out, multiplexer_8_out, multiplexer_9_out, multiplexer_10_out,
       multiplexer_11_out, multiplexer_12_out, multiplexer_13_out, multiplexer_14_out, multiplexer_15_out,
       multiplexer_16_out, multiplexer_17_out, multiplexer_18_out, multiplexer_19_out, multiplexer_20_out,
       multiplexer_21_out, multiplexer_22_out, multiplexer_23_out, multiplexer_24_out, multiplexer_25_out,
       multiplexer_26_out, multiplexer_27_out, multiplexer_28_out, multiplexer_29_out, multiplexer_30_out,
       multiplexer_31_out, multiplexer_32_out, multiplexer_33_out, multiplexer_34_out, multiplexer_35_out,
       multiplexer_36_out, multiplexer_37_out, multiplexer_38_out, multiplexer_39_out, multiplexer_40_out,
       multiplexer_41_out, multiplexer_42_out, multiplexer_43_out, multiplexer_44_out, multiplexer_45_out,
       multiplexer_46_out, multiplexer_47_out, multiplexer_48_out;

  Multiplexer #(.disabled(0), .enable("false")) multiplexer_1 (
    .in0(in_1[0]), .in1(1'b0), .out(multiplexer_1_out), .sel(INPUT[0]));
  Multiplexer #(.disabled(0), .enable("false")) multiplexer_2 (
    .in0(in_1[1]), .in1(in_1[0]), .out(multiplexer_2_out), .sel(INPUT[0]));
  Multiplexer #(.disabled(0), .enable("false")) multiplexer_3 (
    .in0(in_1[2]), .in1(in_1[1]), .out(multiplexer_3_out), .sel(INPUT[0]));
  Multiplexer #(.disabled(0), .enable("false")) multiplexer_4 (
    .in0(in_1[3]), .in1(in_1[2]), .out(multiplexer_4_out), .sel(INPUT[0]));
  Multiplexer #(.disabled(0), .enable("false")) multiplexer_5 (
    .in0(in_1[4]), .in1(in_1[3]), .out(multiplexer_5_out), .sel(INPUT[0]));
  Multiplexer #(.disabled(0), .enable("false")) multiplexer_6 (
    .in0(in_1[5]), .in1(in_1[4]), .out(multiplexer_6_out), .sel(INPUT[0]));
  Multiplexer #(.disabled(0), .enable("false")) multiplexer_7 (
    .in0(in_1[6]), .in1(in_1[5]), .out(multiplexer_7_out), .sel(INPUT[0]));
  Multiplexer #(.disabled(0), .enable("false")) multiplexer_8 (
    .in0(in_1[7]), .in1(in_1[6]), .out(multiplexer_8_out), .sel(INPUT[0]));
  Multiplexer #(.disabled(0), .enable("false")) multiplexer_9 (
    .in0(in_1[8]), .in1(in_1[7]), .out(multiplexer_9_out), .sel(INPUT[0]));
  Multiplexer #(.disabled(0), .enable("false")) multiplexer_10 (
    .in0(in_1[9]), .in1(in_1[8]), .out(multiplexer_10_out), .sel(INPUT[0]));
  Multiplexer #(.disabled(0), .enable("false")) multiplexer_11 (
    .in0(in_1[10]), .in1(in_1[9]), .out(multiplexer_11_out), .sel(INPUT[0]));
  Multiplexer #(.disabled(0), .enable("false")) multiplexer_12 (
    .in0(in_1[11]), .in1(in_1[10]), .out(multiplexer_12_out), .sel(INPUT[0]));
  Multiplexer #(.disabled(0), .enable("false")) multiplexer_13 (
    .in0(in_1[12]), .in1(in_1[11]), .out(multiplexer_13_out), .sel(INPUT[0]));
  Multiplexer #(.disabled(0), .enable("false")) multiplexer_14 (
    .in0(in_1[13]), .in1(in_1[12]), .out(multiplexer_14_out), .sel(INPUT[0]));
  Multiplexer #(.disabled(0), .enable("false")) multiplexer_15 (
    .in0(in_1[14]), .in1(in_1[13]), .out(multiplexer_15_out), .sel(INPUT[0]));
  Multiplexer #(.disabled(0), .enable("false")) multiplexer_16 (
    .in0(in_1[15]), .in1(in_1[14]), .out(multiplexer_16_out), .sel(INPUT[0]));
  Multiplexer #(.disabled(0), .enable("false")) multiplexer_17 (
    .in0(multiplexer_1_out), .in1(1'b0), .out(multiplexer_17_out), .sel(INPUT[1]));
  Multiplexer #(.disabled(0), .enable("false")) multiplexer_18 (
    .in0(multiplexer_2_out), .in1(1'b0), .out(multiplexer_18_out), .sel(INPUT[1]));
  Multiplexer #(.disabled(0), .enable("false")) multiplexer_19 (
    .in0(multiplexer_3_out), .in1(multiplexer_1_out), .out(multiplexer_19_out), .sel(INPUT[1]));
  Multiplexer #(.disabled(0), .enable("false")) multiplexer_20 (
    .in0(multiplexer_4_out), .in1(multiplexer_2_out), .out(multiplexer_20_out), .sel(INPUT[1]));
  Multiplexer #(.disabled(0), .enable("false")) multiplexer_21 (
    .in0(multiplexer_5_out), .in1(multiplexer_3_out), .out(multiplexer_21_out), .sel(INPUT[1]));
  Multiplexer #(.disabled(0), .enable("false")) multiplexer_22 (
    .in0(multiplexer_6_out), .in1(multiplexer_4_out), .out(multiplexer_22_out), .sel(INPUT[1]));
  Multiplexer #(.disabled(0), .enable("false")) multiplexer_23 (
    .in0(multiplexer_7_out), .in1(multiplexer_5_out), .out(multiplexer_23_out), .sel(INPUT[1]));
  Multiplexer #(.disabled(0), .enable("false")) multiplexer_24 (
    .in0(multiplexer_8_out), .in1(multiplexer_6_out), .out(multiplexer_24_out), .sel(INPUT[1]));
  Multiplexer #(.disabled(0), .enable("false")) multiplexer_25 (
    .in0(multiplexer_9_out), .in1(multiplexer_7_out), .out(multiplexer_25_out), .sel(INPUT[1]));
  Multiplexer #(.disabled(0), .enable("false")) multiplexer_26 (
    .in0(multiplexer_10_out), .in1(multiplexer_8_out), .out(multiplexer_26_out), .sel(INPUT[1]));
  Multiplexer #(.disabled(0), .enable("false")) multiplexer_27 (
    .in0(multiplexer_11_out), .in1(multiplexer_9_out), .out(multiplexer_27_out), .sel(INPUT[1]));
  Multiplexer #(.disabled(0), .enable("false")) multiplexer_28 (
    .in0(multiplexer_12_out), .in1(multiplexer_10_out), .out(multiplexer_28_out), .sel(INPUT[1]));
  Multiplexer #(.disabled(0), .enable("false")) multiplexer_29 (
    .in0(multiplexer_13_out), .in1(multiplexer_11_out), .out(multiplexer_29_out), .sel(INPUT[1]));
  Multiplexer #(.disabled(0), .enable("false")) multiplexer_30 (
    .in0(multiplexer_14_out), .in1(multiplexer_12_out), .out(multiplexer_30_out), .sel(INPUT[1]));
  Multiplexer #(.disabled(0), .enable("false")) multiplexer_31 (
    .in0(multiplexer_15_out), .in1(multiplexer_13_out), .out(multiplexer_31_out), .sel(INPUT[1]));
  Multiplexer #(.disabled(0), .enable("false")) multiplexer_32 (
    .in0(multiplexer_16_out), .in1(multiplexer_14_out), .out(multiplexer_32_out), .sel(INPUT[1]));
  Multiplexer #(.disabled(0), .enable("false")) multiplexer_33 (
    .in0(multiplexer_17_out), .in1(1'b0), .out(multiplexer_33_out), .sel(INPUT[2]));
  Multiplexer #(.disabled(0), .enable("false")) multiplexer_34 (
    .in0(multiplexer_18_out), .in1(1'b0), .out(multiplexer_34_out), .sel(INPUT[2]));
  Multiplexer #(.disabled(0), .enable("false")) multiplexer_35 (
    .in0(multiplexer_19_out), .in1(1'b0), .out(multiplexer_35_out), .sel(INPUT[2]));
  Multiplexer #(.disabled(0), .enable("false")) multiplexer_36 (
    .in0(multiplexer_20_out), .in1(1'b0), .out(multiplexer_36_out), .sel(INPUT[2]));
  Multiplexer #(.disabled(0), .enable("false")) multiplexer_37 (
    .in0(multiplexer_21_out), .in1(multiplexer_17_out), .out(multiplexer_37_out), .sel(INPUT[2]));
  Multiplexer #(.disabled(0), .enable("false")) multiplexer_38 (
    .in0(multiplexer_22_out), .in1(multiplexer_18_out), .out(multiplexer_38_out), .sel(INPUT[2]));
  Multiplexer #(.disabled(0), .enable("false")) multiplexer_39 (
    .in0(multiplexer_23_out), .in1(multiplexer_19_out), .out(multiplexer_39_out), .sel(INPUT[2]));
  Multiplexer #(.disabled(0), .enable("false")) multiplexer_40 (
    .in0(multiplexer_24_out), .in1(multiplexer_20_out), .out(multiplexer_40_out), .sel(INPUT[2]));
  Multiplexer #(.disabled(0), .enable("false")) multiplexer_41 (
    .in0(multiplexer_25_out), .in1(multiplexer_21_out), .out(multiplexer_41_out), .sel(INPUT[2]));
  Multiplexer #(.disabled(0), .enable("false")) multiplexer_42 (
    .in0(multiplexer_26_out), .in1(multiplexer_22_out), .out(multiplexer_42_out), .sel(INPUT[2]));
  Multiplexer #(.disabled(0), .enable("false")) multiplexer_43 (
    .in0(multiplexer_27_out), .in1(multiplexer_23_out), .out(multiplexer_43_out), .sel(INPUT[2]));
  Multiplexer #(.disabled(0), .enable("false")) multiplexer_44 (
    .in0(multiplexer_28_out), .in1(multiplexer_24_out), .out(multiplexer_44_out), .sel(INPUT[2]));
  Multiplexer #(.disabled(0), .enable("false")) multiplexer_45 (
    .in0(multiplexer_29_out), .in1(multiplexer_25_out), .out(multiplexer_45_out), .sel(INPUT[2]));
  Multiplexer #(.disabled(0), .enable("false")) multiplexer_46 (
    .in0(multiplexer_30_out), .in1(multiplexer_26_out), .out(multiplexer_46_out), .sel(INPUT[2]));
  Multiplexer #(.disabled(0), .enable("false")) multiplexer_47 (
    .in0(multiplexer_31_out), .in1(multiplexer_27_out), .out(multiplexer_47_out), .sel(INPUT[2]));
  Multiplexer #(.disabled(0), .enable("false")) multiplexer_48 (
    .in0(multiplexer_32_out), .in1(multiplexer_28_out), .out(multiplexer_48_out), .sel(INPUT[2]));
  Multiplexer #(.disabled(0), .enable("false")) multiplexer_49 (
    .in0(multiplexer_33_out), .in1(1'b0), .out(out_3[0]), .sel(INPUT[3]));
  Multiplexer #(.disabled(0), .enable("false")) multiplexer_50 (
    .in0(multiplexer_34_out), .in1(1'b0), .out(out_3[1]), .sel(INPUT[3]));
  Multiplexer #(.disabled(0), .enable("false")) multiplexer_51 (
    .in0(multiplexer_35_out), .in1(1'b0), .out(out_3[2]), .sel(INPUT[3]));
  Multiplexer #(.disabled(0), .enable("false")) multiplexer_52 (
    .in0(multiplexer_36_out), .in1(1'b0), .out(out_3[3]), .sel(INPUT[3]));
  Multiplexer #(.disabled(0), .enable("false")) multiplexer_53 (
    .in0(multiplexer_37_out), .in1(1'b0), .out(out_3[4]), .sel(INPUT[3]));
  Multiplexer #(.disabled(0), .enable("false")) multiplexer_54 (
    .in0(multiplexer_38_out), .in1(1'b0), .out(out_3[5]), .sel(INPUT[3]));
  Multiplexer #(.disabled(0), .enable("false")) multiplexer_55 (
    .in0(multiplexer_39_out), .in1(1'b0), .out(out_3[6]), .sel(INPUT[3]));
  Multiplexer #(.disabled(0), .enable("false")) multiplexer_56 (
    .in0(multiplexer_40_out), .in1(1'b0), .out(out_3[7]), .sel(INPUT[3]));
  Multiplexer #(.disabled(0), .enable("false")) multiplexer_57 (
    .in0(multiplexer_41_out), .in1(multiplexer_33_out), .out(out_3[8]), .sel(INPUT[3]));
  Multiplexer #(.disabled(0), .enable("false")) multiplexer_58 (
    .in0(multiplexer_42_out), .in1(multiplexer_34_out), .out(out_3[9]), .sel(INPUT[3]));
  Multiplexer #(.disabled(0), .enable("false")) multiplexer_59 (
    .in0(multiplexer_43_out), .in1(multiplexer_35_out), .out(out_3[10]), .sel(INPUT[3]));
  Multiplexer #(.disabled(0), .enable("false")) multiplexer_60 (
    .in0(multiplexer_44_out), .in1(multiplexer_36_out), .out(out_3[11]), .sel(INPUT[3]));
  Multiplexer #(.disabled(0), .enable("false")) multiplexer_61 (
    .in0(multiplexer_45_out), .in1(multiplexer_37_out), .out(out_3[12]), .sel(INPUT[3]));
  Multiplexer #(.disabled(0), .enable("false")) multiplexer_62 (
    .in0(multiplexer_46_out), .in1(multiplexer_38_out), .out(out_3[13]), .sel(INPUT[3]));
  Multiplexer #(.disabled(0), .enable("false")) multiplexer_63 (
    .in0(multiplexer_47_out), .in1(multiplexer_39_out), .out(out_3[14]), .sel(INPUT[3]));
  Multiplexer #(.disabled(0), .enable("false")) multiplexer_64 (
    .in0(multiplexer_48_out), .in1(multiplexer_40_out), .out(out_3[15]), .sel(INPUT[3]));
endmodule

// #2
module BALL__DECODER__2 (
  input  [3:0] BALL__position_y,
  input  BALL__enabled,
  input  [3:0] BALL__position_x,
  output [15:0] out_4,
  output [15:0] out_5,
  output [15:0] out_6,
  output [15:0] out_7,
  output [15:0] out_8,
  output [15:0] out_9,
  output [15:0] out_10,
  output [15:0] out_11,
  output [15:0] out_12,
  output [15:0] out_13,
  output [15:0] out_14,
  output [15:0] out_15,
  output [15:0] out_16,
  output [15:0] out_17,
  output [15:0] out_18,
  output [15:0] out_19,
  output [15:0] out_20
);

  wire decoder_2_out0, decoder_2_out1, decoder_2_out2, decoder_2_out3, decoder_2_out4, decoder_2_out5,
       decoder_2_out6, decoder_2_out7, decoder_2_out8, decoder_2_out9, decoder_2_out10, decoder_2_out11,
       decoder_2_out12, decoder_2_out13, decoder_2_out14, decoder_2_out15;
  wire [15:0] adder_1_out, adder_2_out, adder_3_out, adder_4_out, adder_5_out, adder_6_out, adder_7_out,
       adder_8_out, adder_9_out, adder_10_out, adder_11_out, adder_12_out, adder_13_out, adder_14_out;

  Decoder #(.select(4), .disabled(0)) decoder_1 (
    .out0(out_4[0]), .out1(out_4[1]), .out2(out_4[2]), .out3(out_4[3]), .out4(out_4[4]), .out5(out_4[5]),
    .out6(out_4[6]), .out7(out_4[7]), .out8(out_4[8]), .out9(out_4[9]), .out10(out_4[10]), .out11(out_4[11]),
    .out12(out_4[12]), .out13(out_4[13]), .out14(out_4[14]), .out15(out_4[15]), .sel(BALL__position_y),
    .en(decoder_2_out0));
  Decoder #(.select(4), .disabled(0)) decoder_2 (
    .out0(decoder_2_out0), .out1(decoder_2_out1), .out2(decoder_2_out2), .out3(decoder_2_out3),
    .out4(decoder_2_out4), .out5(decoder_2_out5), .out6(decoder_2_out6), .out7(decoder_2_out7),
    .out8(decoder_2_out8), .out9(decoder_2_out9), .out10(decoder_2_out10), .out11(decoder_2_out11),
    .out12(decoder_2_out12), .out13(decoder_2_out13), .out14(decoder_2_out14), .out15(decoder_2_out15),
    .sel(BALL__position_x), .en(BALL__enabled));
  Decoder #(.select(4), .disabled(0)) decoder_3 (
    .out0(out_5[0]), .out1(out_5[1]), .out2(out_5[2]), .out3(out_5[3]), .out4(out_5[4]), .out5(out_5[5]),
    .out6(out_5[6]), .out7(out_5[7]), .out8(out_5[8]), .out9(out_5[9]), .out10(out_5[10]), .out11(out_5[11]),
    .out12(out_5[12]), .out13(out_5[13]), .out14(out_5[14]), .out15(out_5[15]), .sel(BALL__position_y),
    .en(decoder_2_out1));
  Decoder #(.select(4), .disabled(0)) decoder_4 (
    .out0(out_6[0]), .out1(out_6[1]), .out2(out_6[2]), .out3(out_6[3]), .out4(out_6[4]), .out5(out_6[5]),
    .out6(out_6[6]), .out7(out_6[7]), .out8(out_6[8]), .out9(out_6[9]), .out10(out_6[10]), .out11(out_6[11]),
    .out12(out_6[12]), .out13(out_6[13]), .out14(out_6[14]), .out15(out_6[15]), .sel(BALL__position_y),
    .en(decoder_2_out2));
  Decoder #(.select(4), .disabled(0)) decoder_5 (
    .out0(out_7[0]), .out1(out_7[1]), .out2(out_7[2]), .out3(out_7[3]), .out4(out_7[4]), .out5(out_7[5]),
    .out6(out_7[6]), .out7(out_7[7]), .out8(out_7[8]), .out9(out_7[9]), .out10(out_7[10]), .out11(out_7[11]),
    .out12(out_7[12]), .out13(out_7[13]), .out14(out_7[14]), .out15(out_7[15]), .sel(BALL__position_y),
    .en(decoder_2_out3));
  Decoder #(.select(4), .disabled(0)) decoder_6 (
    .out0(out_8[0]), .out1(out_8[1]), .out2(out_8[2]), .out3(out_8[3]), .out4(out_8[4]), .out5(out_8[5]),
    .out6(out_8[6]), .out7(out_8[7]), .out8(out_8[8]), .out9(out_8[9]), .out10(out_8[10]), .out11(out_8[11]),
    .out12(out_8[12]), .out13(out_8[13]), .out14(out_8[14]), .out15(out_8[15]), .sel(BALL__position_y),
    .en(decoder_2_out4));
  Decoder #(.select(4), .disabled(0)) decoder_7 (
    .out0(out_9[0]), .out1(out_9[1]), .out2(out_9[2]), .out3(out_9[3]), .out4(out_9[4]), .out5(out_9[5]),
    .out6(out_9[6]), .out7(out_9[7]), .out8(out_9[8]), .out9(out_9[9]), .out10(out_9[10]), .out11(out_9[11]),
    .out12(out_9[12]), .out13(out_9[13]), .out14(out_9[14]), .out15(out_9[15]), .sel(BALL__position_y),
    .en(decoder_2_out5));
  Decoder #(.select(4), .disabled(0)) decoder_8 (
    .out0(out_10[0]), .out1(out_10[1]), .out2(out_10[2]), .out3(out_10[3]), .out4(out_10[4]),
    .out5(out_10[5]), .out6(out_10[6]), .out7(out_10[7]), .out8(out_10[8]), .out9(out_10[9]),
    .out10(out_10[10]), .out11(out_10[11]), .out12(out_10[12]), .out13(out_10[13]), .out14(out_10[14]),
    .out15(out_10[15]), .sel(BALL__position_y), .en(decoder_2_out6));
  Decoder #(.select(4), .disabled(0)) decoder_9 (
    .out0(out_11[0]), .out1(out_11[1]), .out2(out_11[2]), .out3(out_11[3]), .out4(out_11[4]),
    .out5(out_11[5]), .out6(out_11[6]), .out7(out_11[7]), .out8(out_11[8]), .out9(out_11[9]),
    .out10(out_11[10]), .out11(out_11[11]), .out12(out_11[12]), .out13(out_11[13]), .out14(out_11[14]),
    .out15(out_11[15]), .sel(BALL__position_y), .en(decoder_2_out7));
  Decoder #(.select(4), .disabled(0)) decoder_10 (
    .out0(out_12[0]), .out1(out_12[1]), .out2(out_12[2]), .out3(out_12[3]), .out4(out_12[4]),
    .out5(out_12[5]), .out6(out_12[6]), .out7(out_12[7]), .out8(out_12[8]), .out9(out_12[9]),
    .out10(out_12[10]), .out11(out_12[11]), .out12(out_12[12]), .out13(out_12[13]), .out14(out_12[14]),
    .out15(out_12[15]), .sel(BALL__position_y), .en(decoder_2_out8));
  Decoder #(.select(4), .disabled(0)) decoder_11 (
    .out0(out_13[0]), .out1(out_13[1]), .out2(out_13[2]), .out3(out_13[3]), .out4(out_13[4]),
    .out5(out_13[5]), .out6(out_13[6]), .out7(out_13[7]), .out8(out_13[8]), .out9(out_13[9]),
    .out10(out_13[10]), .out11(out_13[11]), .out12(out_13[12]), .out13(out_13[13]), .out14(out_13[14]),
    .out15(out_13[15]), .sel(BALL__position_y), .en(decoder_2_out9));
  Decoder #(.select(4), .disabled(0)) decoder_12 (
    .out0(out_14[0]), .out1(out_14[1]), .out2(out_14[2]), .out3(out_14[3]), .out4(out_14[4]),
    .out5(out_14[5]), .out6(out_14[6]), .out7(out_14[7]), .out8(out_14[8]), .out9(out_14[9]),
    .out10(out_14[10]), .out11(out_14[11]), .out12(out_14[12]), .out13(out_14[13]), .out14(out_14[14]),
    .out15(out_14[15]), .sel(BALL__position_y), .en(decoder_2_out10));
  Decoder #(.select(4), .disabled(0)) decoder_13 (
    .out0(out_15[0]), .out1(out_15[1]), .out2(out_15[2]), .out3(out_15[3]), .out4(out_15[4]),
    .out5(out_15[5]), .out6(out_15[6]), .out7(out_15[7]), .out8(out_15[8]), .out9(out_15[9]),
    .out10(out_15[10]), .out11(out_15[11]), .out12(out_15[12]), .out13(out_15[13]), .out14(out_15[14]),
    .out15(out_15[15]), .sel(BALL__position_y), .en(decoder_2_out11));
  Decoder #(.select(4), .disabled(0)) decoder_14 (
    .out0(out_16[0]), .out1(out_16[1]), .out2(out_16[2]), .out3(out_16[3]), .out4(out_16[4]),
    .out5(out_16[5]), .out6(out_16[6]), .out7(out_16[7]), .out8(out_16[8]), .out9(out_16[9]),
    .out10(out_16[10]), .out11(out_16[11]), .out12(out_16[12]), .out13(out_16[13]), .out14(out_16[14]),
    .out15(out_16[15]), .sel(BALL__position_y), .en(decoder_2_out12));
  Decoder #(.select(4), .disabled(0)) decoder_15 (
    .out0(out_17[0]), .out1(out_17[1]), .out2(out_17[2]), .out3(out_17[3]), .out4(out_17[4]),
    .out5(out_17[5]), .out6(out_17[6]), .out7(out_17[7]), .out8(out_17[8]), .out9(out_17[9]),
    .out10(out_17[10]), .out11(out_17[11]), .out12(out_17[12]), .out13(out_17[13]), .out14(out_17[14]),
    .out15(out_17[15]), .sel(BALL__position_y), .en(decoder_2_out13));
  Decoder #(.select(4), .disabled(0)) decoder_16 (
    .out0(out_18[0]), .out1(out_18[1]), .out2(out_18[2]), .out3(out_18[3]), .out4(out_18[4]),
    .out5(out_18[5]), .out6(out_18[6]), .out7(out_18[7]), .out8(out_18[8]), .out9(out_18[9]),
    .out10(out_18[10]), .out11(out_18[11]), .out12(out_18[12]), .out13(out_18[13]), .out14(out_18[14]),
    .out15(out_18[15]), .sel(BALL__position_y), .en(decoder_2_out14));
  Decoder #(.select(4), .disabled(0)) decoder_17 (
    .out0(out_19[0]), .out1(out_19[1]), .out2(out_19[2]), .out3(out_19[3]), .out4(out_19[4]),
    .out5(out_19[5]), .out6(out_19[6]), .out7(out_19[7]), .out8(out_19[8]), .out9(out_19[9]),
    .out10(out_19[10]), .out11(out_19[11]), .out12(out_19[12]), .out13(out_19[13]), .out14(out_19[14]),
    .out15(out_19[15]), .sel(BALL__position_y), .en(decoder_2_out15));
  Adder #(.width(16)) adder_1 (.a(out_19), .b(out_18), .out(adder_1_out));  // open: cin, cout
  Adder #(.width(16)) adder_2 (.a(out_17), .b(out_16), .out(adder_2_out));  // open: cin, cout
  Adder #(.width(16)) adder_3 (.a(out_15), .b(out_14), .out(adder_3_out));  // open: cin, cout
  Adder #(.width(16)) adder_4 (.a(out_13), .b(out_12), .out(adder_4_out));  // open: cin, cout
  Adder #(.width(16)) adder_5 (.a(out_11), .b(out_10), .out(adder_5_out));  // open: cin, cout
  Adder #(.width(16)) adder_6 (.a(out_9), .b(out_8), .out(adder_6_out));  // open: cin, cout
  Adder #(.width(16)) adder_7 (.a(out_7), .b(out_6), .out(adder_7_out));  // open: cin, cout
  Adder #(.width(16)) adder_8 (.a(out_5), .b(out_4), .out(adder_8_out));  // open: cin, cout
  Adder #(.width(16)) adder_9 (.a(adder_1_out), .b(adder_2_out), .out(adder_9_out));  // open: cin, cout
  Adder #(.width(16)) adder_10 (.a(adder_3_out), .b(adder_4_out), .out(adder_10_out));  // open: cin, cout
  Adder #(.width(16)) adder_11 (.a(adder_5_out), .b(adder_6_out), .out(adder_11_out));  // open: cin, cout
  Adder #(.width(16)) adder_12 (.a(adder_7_out), .b(adder_8_out), .out(adder_12_out));  // open: cin, cout
  Adder #(.width(16)) adder_13 (.a(adder_9_out), .b(adder_10_out), .out(adder_13_out));  // open: cin, cout
  Adder #(.width(16)) adder_14 (.a(adder_11_out), .b(adder_12_out), .out(adder_14_out));  // open: cin, cout
  // Probe on out_20
  Adder #(.width(16)) adder_15 (.a(adder_13_out), .b(adder_14_out), .out(out_20));  // open: cin, cout
endmodule

// #3
module BALL__COLLISION__3 (
  input  [3:0] BOARD__position,
  input  BALL__x___1,
  input  Y__direction,
  input  [3:0] BALL__y,
  output OUTPUT
);

  wire and_1_out, and_2_out, and_3_out, and_5_out, and_6_out, and_7_out, comparator_1_eq, comparator_1_gt,
       comparator_2_eq, comparator_2_lt, nor_1_out, nor_2_out, or_1_out, or_2_out, or_3_out;
  wire [3:0] adder_1_out, adder_2_out;
  wire [3:3] and_4_out;

  // Probe on BALL__y
  // Probe on BOARD__position
  and and_1 (and_1_out, BOARD__position[3], BOARD__position[2], ~BOARD__position[1], ~BOARD__position[0]);  // AND_Gate
  nor nor_1 (nor_1_out, BOARD__position[3], BOARD__position[2], BOARD__position[1], BOARD__position[0]);
  and and_2 (and_2_out, nor_1_out, nor_2_out);
  nor nor_2 (nor_2_out, BALL__y[0], BALL__y[1], BALL__y[2], BALL__y[3]);
  and and_3 (and_3_out, BALL__y[0], BALL__y[1], BALL__y[2], BALL__y[3]);
  and and_4 (and_4_out[3], ~nor_2_out, ~Y__direction);  // AND_Gate
  // Probe on adder_1_out
  Adder #(.width(4)) adder_1 (.a(4'b0011), .b(BOARD__position), .out(adder_1_out));  // open: cin, cout
  and and_5 (and_5_out, and_1_out, and_3_out);
  and and_6 (and_6_out, Y__direction, ~and_3_out);  // AND_Gate
  // Probe on adder_2_out
  Adder #(.width(4)) adder_2 (.a(BALL__y), .b({4{and_4_out[3]}}), .out(adder_2_out), .cin(and_6_out));  // open: cout
  or or_1 (or_1_out, comparator_1_gt, comparator_1_eq);
  Comparator #(.width(4), .mode("unsigned")) comparator_1 (
    .a(adder_1_out), .b(adder_2_out), .gt(comparator_1_gt), .eq(comparator_1_eq));  // open: lt
  or or_2 (or_2_out, comparator_2_eq, comparator_2_lt);
  Comparator #(.width(4), .mode("unsigned")) comparator_2 (
    .a(BOARD__position), .b(adder_2_out), .eq(comparator_2_eq), .lt(comparator_2_lt));  // open: gt
  and and_7 (and_7_out, or_1_out, or_2_out);
  or or_3 (or_3_out, and_7_out, and_5_out, and_2_out);
  and and_8 (OUTPUT, ~or_3_out, BALL__x___1);  // AND_Gate
endmodule

// #4
module GAME__STATE__4 (
  input  in_1,
  input  in_2,
  input  in_3,
  output [8:0] out_4,
  output [8:0] out_5,
  output [8:0] out_6,
  output [8:0] out_7,
  output [8:0] out_8,
  output [8:0] out_9,
  output [8:0] out_10,
  output [8:0] out_11,
  output [8:0] out_12,
  output [8:0] out_13,
  output [8:0] out_14,
  output [8:0] out_15,
  output [8:0] out_16,
  output [8:0] out_17,
  output [8:0] out_18,
  output [8:0] out_19,
  output [8:0] out_20,
  output [8:0] out_21,
  output [8:0] out_22,
  output [8:0] out_23,
  output [8:0] out_24,
  output [8:0] out_25,
  output [8:0] out_26,
  output [8:0] out_27,
  output [8:0] out_28
);

  wire and_1_out, and_2_out, and_3_out, and_4_out, clock_1_out, xor_1_out;
  wire [4:0] counter_1_q, counter_2_q;
  wire [8:0] rom_1_data, rom_2_data;

  LED led_1 (.in(in_1));
  Register #(.width(9)) register_1 (.D(out_7), .Q(out_6), .clk(xor_1_out), .clr(in_1));  // open: en
  Register #(.width(9)) register_2 (.D(out_6), .Q(out_5), .clk(xor_1_out), .clr(in_1));  // open: en
  Register #(.width(9)) register_3 (.D(out_5), .Q(out_4), .clk(xor_1_out), .clr(in_1));  // open: en
  Register #(.width(9)) register_4 (.D(out_8), .Q(out_7), .clk(xor_1_out), .clr(in_1));  // open: en
  Register #(.width(9)) register_5 (.D(out_9), .Q(out_8), .clk(xor_1_out), .clr(in_1));  // open: en
  Register #(.width(9)) register_6 (.D(out_10), .Q(out_9), .clk(xor_1_out), .clr(in_1));  // open: en
  Register #(.width(9)) register_7 (.D(out_13), .Q(out_12), .clk(xor_1_out), .clr(in_1));  // open: en
  Register #(.width(9)) register_8 (.D(out_12), .Q(out_11), .clk(xor_1_out), .clr(in_1));  // open: en
  Register #(.width(9)) register_9 (.D(out_11), .Q(out_10), .clk(xor_1_out), .clr(in_1));  // open: en
  Register #(.width(9)) register_10 (.D(out_14), .Q(out_13), .clk(xor_1_out), .clr(in_1));  // open: en
  Register #(.width(9)) register_11 (.D(out_15), .Q(out_14), .clk(xor_1_out), .clr(in_1));  // open: en
  Register #(.width(9)) register_12 (.D(out_16), .Q(out_15), .clk(xor_1_out), .clr(in_1));  // open: en
  Register #(.width(9)) register_13 (.D(out_19), .Q(out_18), .clk(xor_1_out), .clr(in_1));  // open: en
  Register #(.width(9)) register_14 (.D(out_18), .Q(out_17), .clk(xor_1_out), .clr(in_1));  // open: en
  Register #(.width(9)) register_15 (.D(out_17), .Q(out_16), .clk(xor_1_out), .clr(in_1));  // open: en
  Register #(.width(9)) register_16 (.D(out_20), .Q(out_19), .clk(xor_1_out), .clr(in_1));  // open: en
  Register #(.width(9)) register_17 (.D(out_21), .Q(out_20), .clk(xor_1_out), .clr(in_1));  // open: en
  Register #(.width(9)) register_18 (.D(out_22), .Q(out_21), .clk(xor_1_out), .clr(in_1));  // open: en
  Register #(.width(9)) register_19 (.D(out_25), .Q(out_24), .clk(xor_1_out), .clr(in_1));  // open: en
  Register #(.width(9)) register_20 (.D(out_24), .Q(out_23), .clk(xor_1_out), .clr(in_1));  // open: en
  Register #(.width(9)) register_21 (.D(out_23), .Q(out_22), .clk(xor_1_out), .clr(in_1));  // open: en
  Clock clock_1 (.out(clock_1_out));
  Register #(.width(9)) register_22 (.D(out_26), .Q(out_25), .clk(xor_1_out), .clr(in_1));  // open: en
  Register #(.width(9)) register_23 (.D(out_27), .Q(out_26), .clk(xor_1_out), .clr(in_1));  // open: en
  Register #(.width(9)) register_24 (.D(out_28), .Q(out_27), .clk(xor_1_out), .clr(in_1));  // open: en
  and and_1 (and_1_out, in_2, clock_1_out);
  and and_2 (and_2_out, clock_1_out, in_3);
  LED led_2 (.in(in_3));
  Counter #(.width(5), .max('h1f)) counter_1 (
    .Q(counter_1_q), .clk(and_3_out), .clr(in_1));  // open: load, D, count, carry
  xor xor_1 (xor_1_out, and_3_out, and_4_out);
  and and_3 (and_3_out, and_1_out, ~in_3);  // AND_Gate
  and and_4 (and_4_out, ~in_2, and_2_out);  // AND_Gate
  Counter #(.width(5), .max('h1f)) counter_2 (
    .Q(counter_2_q), .clk(and_4_out), .clr(in_1));  // open: load, D, count, carry
  ROM #(.addrWidth(5), .dataWidth(9)) rom_1 (.addr(counter_1_q), .data(rom_1_data));  // open: sel
  ROM #(.addrWidth(5), .dataWidth(9)) rom_2 (.addr(counter_2_q), .data(rom_2_data));  // open: sel
  assign out_28 = rom_1_data ^ rom_2_data;  // XOR_Gate xor_2, 9 bits wide

  // Notes on the sheet:
  //   contents of rom_1 (hex, n*v repeats v):
  //   0 c0 3e c0 0 fe 82 fe 0 fe 2 fe 0 0 0 fe 2 2 0 fe 82 fe 0 e2 92 8e 0 80 fe 80
  //   contents of rom_2 (hex, n*v repeats v):
  //   0 c0 3e c0 0 fe 82 fe 0 fe 2 fe 0 0 0 fe 2 fe 2 fe 0 fe 0 fe 20 10 8 fe
endmodule

// #5
module GAME__CONTROLLER__5 (
  input  [6:0] in_1,
  input  Start,
  output [15:0] out_3,
  output [3:0] out_4
);

  wire and_1_out, clock_1_out, comparator_1_eq, comparator_2_eq, comparator_3_eq, comparator_4_eq;
  wire [3:0] adder_1_out, register_1_q;
  wire [3:3] and_2_out;

  Comparator #(.width(7), .mode("unsigned")) comparator_1 (
    .a(7'b1100001), .b(in_1), .eq(comparator_1_eq));  // open: gt, lt
  Comparator #(.width(7), .mode("unsigned")) comparator_2 (
    .a(in_1), .b(7'b1100100), .eq(comparator_2_eq));  // open: gt, lt
  and and_1 (and_1_out, ~comparator_3_eq, comparator_1_eq, ~and_2_out[3]);  // AND_Gate
  and and_2 (and_2_out[3], ~and_1_out, comparator_2_eq, ~comparator_4_eq);  // AND_Gate
  Adder #(.width(4)) adder_1 (
    .a(register_1_q), .b({4{and_2_out[3]}}), .out(adder_1_out), .cin(and_1_out));  // open: cout
  Register #(.width(4)) register_1 (.D(adder_1_out), .Q(register_1_q), .clk(clock_1_out), .clr(Start));  // open: en
  Clock clock_1 (.out(clock_1_out));
  BALL__SHIFTER__1 ball_shifter__1_1 (.in_1(16'hf), .INPUT(out_4), .out_3(out_3));
  Adder #(.width(4)) adder_2 (.a(register_1_q), .b(4'b0110), .out(out_4));  // open: cin, cout
  Comparator #(.width(4), .mode("unsigned")) comparator_3 (
    .a(4'b1100), .b(out_4), .eq(comparator_3_eq));  // open: gt, lt
  Comparator #(.width(4), .mode("unsigned")) comparator_4 (
    .a(out_4), .b(4'b0000), .eq(comparator_4_eq));  // open: gt, lt

  // Notes on the sheet:
  //   kontroler planszy
endmodule

// #6
module GAME__INIT__6 (
  input  in_1,
  input  in_2,
  input  in_3,
  output out_4,
  output [3:0] out_5,
  output out_6,
  output out_7
);

  wire and_1_out, d_ff_3_q, d_ff_4_q, d_ff_5_q, d_ff_6_q, not_1_out, not_2_out, not_3_out, or_2_out;

  D_Flip_Flop d_ff_1 (.clk(in_1), .D(1'b0), .Q(out_7), .preset(in_3));  // open: Qn, en, reset
  D_Flip_Flop d_ff_2 (.clk(in_1), .D(1'b1), .Q(out_4), .en(d_ff_6_q), .reset(in_3));  // open: Qn, preset
  Counter #(.width(4), .max('hf)) counter_1 (.Q(out_5), .clk(in_2));  // open: load, D, count, carry, clr
  not not_1 (not_1_out, out_4);
  D_Flip_Flop d_ff_3 (.clk(in_2), .D(not_1_out), .Q(d_ff_3_q), .en(not_2_out));  // open: Qn, preset, reset
  not not_2 (not_2_out, d_ff_5_q);
  D_Flip_Flop d_ff_4 (.clk(d_ff_5_q), .D(1'b1), .Q(d_ff_4_q), .reset(in_3));  // open: Qn, preset, en
  or or_1 (out_6, and_1_out, d_ff_5_q);
  and and_1 (and_1_out, out_4, in_2);
  D_Flip_Flop d_ff_5 (.clk(in_2), .D(d_ff_3_q), .Q(d_ff_5_q), .en(not_3_out), .reset(or_2_out));  // open: Qn, preset
  not not_3 (not_3_out, d_ff_4_q);
  D_Flip_Flop d_ff_6 (.clk(in_2), .D(d_ff_4_q), .Q(d_ff_6_q));  // open: Qn, preset, en, reset
  or or_2 (or_2_out, d_ff_6_q, in_1);

  // Notes on the sheet:
  //   część inicjalizująca
endmodule

// #7
module BALL__AXIS__X__7 (
  input  in_1,
  input  in_2,
  input  [3:0] in_3,
  output out_4,
  output [3:0] out_5,
  output out_6
);

  wire and_2_out, and_3_out, nor_1_out;
  wire [3:0] adder_1_out, multiplexer_1_out, or_1_out;

  D_Flip_Flop d_ff_1 (.Q(out_6), .preset(nor_1_out), .reset(and_3_out));  // open: clk, D, Qn, en
  and and_1 (or_1_out[3], ~out_6, in_2);  // AND_Gate
  or or_1 (or_1_out[0], or_1_out[3], and_2_out);
  and and_2 (and_2_out, in_2, out_6);
  Adder #(.width(4)) adder_1 (.a(out_5), .b({{3{or_1_out[3]}}, or_1_out[0]}), .out(adder_1_out));  // open: cin, cout
  Register #(.width(4)) register_1 (.D(multiplexer_1_out), .Q(out_5), .clk(in_1));  // open: en, clr
  Multiplexer #(.width(4), .disabled(0), .enable("false")) multiplexer_1 (
    .in0(in_3), .in1(adder_1_out), .out(multiplexer_1_out), .sel(in_2));
  and and_3 (and_3_out, out_5[3], out_5[2], out_5[1], out_5[0]);
  nor nor_1 (nor_1_out, out_5[3], out_5[2], out_5[1], out_5[0]);

  assign out_4 = in_2;

  // Notes on the sheet:
  //   kontroler piłki osi X
endmodule

// #8
module BALL__AXIS__Y__8 (
  input  in_1,
  input  in_2,
  input  in_3,
  input  in_4,
  output [3:0] out_5,
  output out_6,
  output out_7
);

  wire and_2_out, and_3_out, and_4_out, d_ff_1_q, d_ff_3_q, d_ff_4_q, nor_2_out, or_2_out;
  wire [3:0] adder_1_out, multiplexer_1_out, or_1_out;

  D_Flip_Flop d_ff_1 (.Q(d_ff_1_q), .preset(or_2_out), .reset(and_3_out));  // open: clk, D, Qn, en
  and and_1 (or_1_out[3], ~d_ff_1_q, in_4);  // AND_Gate
  or or_1 (or_1_out[0], or_1_out[3], and_2_out);
  and and_2 (and_2_out, in_4, d_ff_1_q);
  Adder #(.width(4)) adder_1 (.a(out_5), .b({{3{or_1_out[3]}}, or_1_out[0]}), .out(adder_1_out));  // open: cin, cout
  Register #(.width(4)) register_1 (.D(multiplexer_1_out), .Q(out_5), .clk(in_3), .clr(out_7));  // open: en
  Multiplexer #(.width(4), .disabled(0), .enable("false")) multiplexer_1 (
    .in0(4'b0001), .in1(adder_1_out), .out(multiplexer_1_out), .sel(in_4));
  and and_3 (and_3_out, out_5[3], out_5[2], out_5[1], out_5[0]);
  or or_2 (or_2_out, nor_2_out, d_ff_4_q, out_7);
  nor nor_1 (out_6, d_ff_1_q, out_5[3], out_5[2], out_5[1], ~out_5[0]);  // NOR_Gate
  nor nor_2 (nor_2_out, out_5[3], out_5[2], out_5[1], out_5[0]);
  and and_4 (and_4_out, out_6, ~in_1);  // AND_Gate
  D_Flip_Flop d_ff_2 (.clk(in_2), .D(d_ff_3_q), .Q(out_7));  // open: Qn, preset, en, reset
  D_Flip_Flop d_ff_3 (.clk(in_2), .D(in_1), .Q(d_ff_3_q));  // open: Qn, preset, en, reset
  D_Flip_Flop #(.trigger("falling")) d_ff_4 (.clk(in_2), .D(and_4_out), .Q(d_ff_4_q));  // open: Qn, preset, en, reset

  // Notes on the sheet:
  //   kontroler piłki osi Y
endmodule

// #9
module GAME__SCORE__HIGHEST__9 (
  input  [7:0] in_1,
  input  [7:0] in_2,
  input  in_3,
  input  in_4,
  output [7:0] out_5
);

  wire comparator_1_gt, controlled_buffer_2_out, or_1_out;
  wire [7:0] controlled_buffer_1_out;

  assign controlled_buffer_1_out = comparator_1_gt ? in_1 : 8'bz;  // Controlled_Buffer controlled_buffer_1
  Comparator #(.mode("unsigned")) comparator_1 (.a(in_1), .b(in_2), .gt(comparator_1_gt));  // open: eq, lt
  or or_1 (or_1_out, in_3, in_4);
  assign controlled_buffer_2_out = comparator_1_gt ? or_1_out : 1'bz;  // Controlled_Buffer controlled_buffer_2
  RAM #(.bus("separate")) ram_1 (
    .addr({8{1'b0}}), .din(controlled_buffer_1_out), .data(out_5), .clk(controlled_buffer_2_out));  // open: str, sel, ld, clr

  // Notes on the sheet:
  //   Moduł najwyższego wyniku
endmodule

// #10
module GAME__START__10 (
  input  in_1,
  output out_2
);

  wire utility_delay__17_1_out_4, utility_delay__17_2_out_4, utility_delay__17_3_out_4;

  UTILITY__DELAY__17 utility_delay__17_1 (.in_1(in_1), .in_2(8'h2), .out_4(utility_delay__17_1_out_4));  // open: out_3
  UTILITY__DELAY__17 utility_delay__17_2 (
    .in_1(utility_delay__17_1_out_4), .in_2(8'h2), .out_4(utility_delay__17_2_out_4));  // open: out_3
  ExactlyOne xor_1 (
    .out(out_2), .in0(in_1), .in1(utility_delay__17_1_out_4), .in2(utility_delay__17_2_out_4),
    .in3(utility_delay__17_3_out_4));
  UTILITY__DELAY__17 utility_delay__17_3 (
    .in_1(utility_delay__17_2_out_4), .in_2(8'h2), .out_4(utility_delay__17_3_out_4));  // open: out_3
endmodule

// #11
module GAME__BLOCKS__11 (
  input  [3:0] in_1,
  input  [3:0] in_2,
  input  [15:0] in_3,
  input  in_4,
  input  in_5,
  output [15:0] out_6,
  output [3:0] out_7,
  output [3:0] out_8,
  output [15:0] out_9,
  output [15:0] out_10
);

  wire and_1_out, and_2_out, and_3_out, comparator_1_gt, comparator_2_eq, comparator_3_eq, comparator_3_lt,
       or_1_out, or_2_out, utility_delay__17_1_out_4;
  wire [15:0] bit_extender_1_out, multiplexer_1_out, subtractor_1_out;

  // Probe on in_3
  assign bit_extender_1_out = {{12{1'b0}}, in_1};  // Bit_Extender bit_extender_1
  // Probe on subtractor_1_out
  // Probe on out_6
  Subtractor #(.width(16)) subtractor_1 (.a(out_6), .b(in_3), .out(subtractor_1_out));  // open: bin, bout
  Comparator #(.width(16), .mode("unsigned")) comparator_1 (
    .a(out_6), .b(bit_extender_1_out), .gt(comparator_1_gt));  // open: eq, lt
  Comparator #(.width(4), .mode("unsigned")) comparator_2 (
    .a(in_2), .b(4'b1111), .eq(comparator_2_eq));  // open: gt, lt
  Comparator #(.width(4), .mode("unsigned")) comparator_3 (
    .a(in_1), .b(4'b1111), .eq(comparator_3_eq), .lt(comparator_3_lt));  // open: gt
  and and_1 (and_1_out, comparator_2_eq, or_1_out);
  or or_1 (or_1_out, comparator_3_eq, comparator_3_lt);
  Multiplexer #(.width(16), .disabled(0), .enable("false")) multiplexer_1 (
    .in0({16{1'b1}}), .in1(subtractor_1_out), .out(multiplexer_1_out), .sel(in_5));
  and and_2 (and_2_out, comparator_1_gt, and_1_out);
  Counter #(.width(16), .max('hffff), .ongoal("stay")) counter_1 (
    .load(1'b1), .D(multiplexer_1_out), .count(1'b0), .Q(out_6), .clk(or_2_out));  // open: carry, clr
  UTILITY__DELAY__17 utility_delay__17_1 (
    .in_1(and_2_out), .in_2(8'h1), .out_4(utility_delay__17_1_out_4));  // open: out_3
  or or_2 (or_2_out, utility_delay__17_1_out_4, and_3_out);
  and and_3 (and_3_out, ~in_5, in_4);  // AND_Gate

  assign out_7 = in_1;
  assign out_8 = in_2;
  assign out_9 = out_6;
  assign out_10 = out_6;
endmodule

// #12
module GAME__SCORE__CONDITION__12 (
  input  [3:0] in_1,
  input  in_2,
  input  in_3,
  input  [15:0] in_4,
  output [3:0] out_5,
  output [3:0] out_6,
  output out_7,
  output out_8
);

  wire and_1_out, and_2_out, comparator_1_eq, comparator_2_eq, comparator_3_eq, comparator_4_eq,
       comparator_5_eq, or_1_out, utility_delay__17_1_out_4;

  Counter #(.width(4), .max('hf)) counter_1 (
    .Q(out_5), .clk(comparator_2_eq), .clr(and_1_out));  // open: load, D, count, carry
  Counter #(.width(4), .max('hf)) counter_2 (
    .Q(out_6), .clk(comparator_1_eq), .clr(or_1_out));  // open: load, D, count, carry
  or or_1 (or_1_out, and_1_out, comparator_2_eq);
  Comparator #(.width(4), .mode("unsigned")) comparator_1 (
    .a(in_1), .b(4'b1111), .eq(comparator_1_eq));  // open: gt, lt
  Comparator #(.width(4), .mode("unsigned")) comparator_2 (
    .a(out_6), .b(4'b1010), .eq(comparator_2_eq));  // open: gt, lt
  Comparator #(.width(4), .mode("unsigned")) comparator_3 (
    .a(4'b0111), .b(out_6), .eq(comparator_3_eq));  // open: gt, lt
  Comparator #(.width(4), .mode("unsigned")) comparator_4 (
    .a(out_5), .b(4'b0000), .eq(comparator_4_eq));  // open: gt, lt
  and and_1 (and_1_out, ~in_2, in_3);  // AND_Gate
  and and_2 (and_2_out, comparator_3_eq, comparator_4_eq);
  Comparator #(.width(16), .mode("unsigned")) comparator_5 (
    .a(in_4), .b({16{1'b0}}), .eq(comparator_5_eq));  // open: gt, lt
  or or_2 (out_8, and_2_out, comparator_5_eq);
  D_Flip_Flop d_ff_1 (.clk(out_8), .D(out_8), .Q(out_7), .reset(utility_delay__17_1_out_4));  // open: Qn, preset, en
  UTILITY__DELAY__17 utility_delay__17_1 (.in_1(out_7), .in_2(8'h1), .out_4(utility_delay__17_1_out_4));  // open: out_3
endmodule

// #13
module BOARD__CONTROLLER__13 (
  input  [6:0] in_1,
  input  in_2,
  input  in_3,
  input  in_4,
  input  in_5,
  output [15:0] out_6,
  output [15:0] out_7,
  output [15:0] out_8,
  output [15:0] out_9,
  output [15:0] out_10,
  output [15:0] out_11,
  output [15:0] out_12,
  output [15:0] out_13,
  output [15:0] out_14,
  output [15:0] out_15,
  output [15:0] out_16,
  output [15:0] out_17,
  output [15:0] out_18,
  output [15:0] out_19,
  output [15:0] out_20,
  output out_21,
  output [15:0] out_22,
  output out_23,
  output out_24,
  output [3:0] out_25,
  output [3:0] out_26,
  output [15:0] out_27,
  output out_28,
  output out_29,
  output out_30,
  output out_31
);

  wire ball_axis_x__7_1_out_4, ball_axis_x__7_1_out_6, ball_axis_y__8_1_out_6, ball_axis_y__8_1_out_7,
       ball_collision__3_1_output, clock_1_out, game_init__6_1_out_6, game_init__6_1_out_7, or_1_out;
  wire [3:0] game_controller__5_1_out_4, game_init__6_1_out_5;
  wire [15:0] ball_decoder__2_1_out_4, game_controller__5_1_out_3;

  GAME__CONTROLLER__5 game_controller__5_1 (
    .out_3(game_controller__5_1_out_3), .out_4(game_controller__5_1_out_4), .in_1(in_1), .Start(in_2));
  BALL__COLLISION__3 ball_collision__3_1 (
    .BOARD__position(game_controller__5_1_out_4), .BALL__x___1(ball_axis_y__8_1_out_6),
    .Y__direction(ball_axis_x__7_1_out_6), .BALL__y(out_26), .OUTPUT(ball_collision__3_1_output));
  BALL__AXIS__Y__8 ball_axis_y__8_1 (
    .out_5(out_25), .out_6(ball_axis_y__8_1_out_6), .in_1(ball_collision__3_1_output),
    .out_7(ball_axis_y__8_1_out_7), .in_2(clock_1_out), .in_3(game_init__6_1_out_6), .in_4(out_28));
  assign out_22 = game_controller__5_1_out_3 ^ ball_decoder__2_1_out_4;  // XOR_Gate xor_1, 16 bits wide
  BALL__DECODER__2 ball_decoder__2_1 (
    .BALL__position_y(out_26), .BALL__position_x(out_25), .out_4(ball_decoder__2_1_out_4), .out_5(out_19),
    .out_6(out_17), .out_7(out_15), .out_8(out_13), .out_9(out_11), .out_10(out_9), .out_11(out_7),
    .out_12(out_6), .out_13(out_8), .out_14(out_10), .out_15(out_12), .out_16(out_14), .out_17(out_16),
    .out_18(out_18), .out_19(out_20), .BALL__enabled(ball_axis_x__7_1_out_4), .out_20(out_27));
  // Probe on ball_axis_y__8_1_out_7
  Clock #(.highDuration(2), .lowDuration(2)) clock_1 (.out(clock_1_out));
  or or_1 (or_1_out, ball_axis_y__8_1_out_7, in_4);
  // Probe on or_1_out
  BALL__AXIS__X__7 ball_axis_x__7_1 (
    .out_4(ball_axis_x__7_1_out_4), .out_5(out_26), .out_6(ball_axis_x__7_1_out_6),
    .in_3(game_init__6_1_out_5), .in_2(out_28), .in_1(game_init__6_1_out_6));
  // Probe on game_init__6_1_out_5
  GAME__INIT__6 game_init__6_1 (
    .in_1(in_3), .in_2(clock_1_out), .in_3(or_1_out), .out_7(game_init__6_1_out_7),
    .out_5(game_init__6_1_out_5), .out_4(out_28), .out_6(game_init__6_1_out_6));
  // Probe on out_27
  xor xor_2 (out_21, game_init__6_1_out_7, in_5);

  assign out_23 = in_5;
  assign out_24 = in_3;
  assign out_29 = out_21;
  assign out_30 = in_3;
  assign out_31 = in_5;
endmodule

// #14
module GAME__SYSTEM__BASIC__14 (
  input  in_1,
  input  [7:0] in_2,
  input  [7:0] in_3,
  input  in_4,
  input  in_5,
  output [7:0] out_6,
  output out_7
);

  GAME__START__10 game_start__10_1 (.in_1(in_1), .out_2(out_7));
  GAME__SCORE__HIGHEST__9 game_score_highest__9_1 (.in_1(in_2), .in_2(in_3), .in_3(in_4), .in_4(in_5), .out_5(out_6));
endmodule

// #15
module GAME__WIN__CONDITION__15 (
  input  in_1,
  input  [15:0] in_2,
  input  [3:0] in_3,
  input  [3:0] in_4,
  input  [3:0] in_5,
  input  in_6,
  input  in_7,
  input  in_8,
  output [15:0] out_9,
  output [7:0] out_10,
  output [3:0] out_11,
  output [3:0] out_12,
  output out_13,
  output out_14
);

  wire [15:0] game_blocks__11_1_out_9;

  GAME__BLOCKS__11 game_blocks__11_1 (
    .in_1(in_4), .in_3(in_2), .in_2(in_5), .out_6(out_9), .in_5(in_7), .in_4(in_8),
    .out_9(game_blocks__11_1_out_9));  // open: out_7, out_8, out_10
  GAME__SCORE__CONDITION__12 game_score_condition__12_1 (
    .in_1(in_3), .in_4(game_blocks__11_1_out_9), .out_5(out_10[7:4]), .out_6(out_10[3:0]), .in_2(in_1),
    .out_7(out_13), .in_3(in_6), .out_8(out_14));

  assign out_11 = out_10[7:4];
  assign out_12 = out_10[3:0];
endmodule

// #16
module GAME__SYSTEM__16 (
  input  in_1,
  input  [6:0] in_2,
  input  [3:0] in_3,
  input  [15:0] in_4,
  input  in_5,
  input  [3:0] in_6,
  input  in_7,
  input  [3:0] in_8,
  input  in_9,
  input  in_10,
  input  in_11,
  input  in_12,
  input  [7:0] in_13,
  input  [7:0] in_14,
  input  in_15,
  input  in_16,
  output [8:0] out_17,
  output [8:0] out_18,
  output [8:0] out_19,
  output [8:0] out_20,
  output [8:0] out_21,
  output [8:0] out_22,
  output [8:0] out_23,
  output [8:0] out_24,
  output [8:0] out_25,
  output [8:0] out_26,
  output [8:0] out_27,
  output [8:0] out_28,
  output [8:0] out_29,
  output [8:0] out_30,
  output [8:0] out_31,
  output [8:0] out_32,
  output [8:0] out_33,
  output [8:0] out_34,
  output [8:0] out_35,
  output [8:0] out_36,
  output [15:0] out_37,
  output [15:0] out_38,
  output [8:0] out_39,
  output [8:0] out_40,
  output [15:0] out_41,
  output [15:0] out_42,
  output [8:0] out_43,
  output [15:0] out_44,
  output [15:0] out_45,
  output [8:0] out_46,
  output [15:0] out_47,
  output [15:0] out_48,
  output [8:0] out_49,
  output [15:0] out_50,
  output [15:0] out_51,
  output [15:0] out_52,
  output [15:0] out_53,
  output [15:0] out_54,
  output [15:0] out_55,
  output [15:0] out_56,
  output [15:0] out_57,
  output [15:0] out_58,
  output out_59,
  output out_60,
  output [7:0] out_61,
  output [15:0] out_62,
  output out_63,
  output [3:0] out_64,
  output [3:0] out_65,
  output [3:0] out_66,
  output [3:0] out_67,
  output out_68,
  output [7:0] out_69,
  output out_70
);

  wire board_controller__13_1_out_21, board_controller__13_1_out_23, board_controller__13_1_out_24,
       game_win_condition__15_1_out_13, game_win_condition__15_1_out_14;

  GAME__WIN__CONDITION__15 game_win_condition__15_1 (
    .in_3(in_8), .in_4(in_6), .in_2(in_4), .in_5(in_3), .out_11(out_64), .out_12(out_65), .in_1(in_7),
    .in_7(in_10), .in_8(in_11), .in_6(in_9), .out_9(out_51), .out_10(out_61),
    .out_13(game_win_condition__15_1_out_13), .out_14(game_win_condition__15_1_out_14));
  BOARD__CONTROLLER__13 board_controller__13_1 (
    .out_7(out_38), .out_9(out_42), .out_11(out_45), .out_13(out_48), .out_15(out_52), .out_17(out_54),
    .out_19(out_56), .out_21(board_controller__13_1_out_21), .out_22(out_58),
    .out_23(board_controller__13_1_out_23), .out_24(board_controller__13_1_out_24), .in_1(in_2),
    .in_4(game_win_condition__15_1_out_13), .in_5(game_win_condition__15_1_out_14), .in_3(in_1), .in_2(in_5),
    .out_25(out_67), .out_26(out_66), .out_28(out_68), .out_27(out_62), .out_30(out_63), .out_6(out_57),
    .out_8(out_55), .out_10(out_53), .out_12(out_50), .out_14(out_47), .out_16(out_44), .out_18(out_41),
    .out_20(out_37), .out_29(out_59), .out_31(out_60));
  GAME__STATE__4 game_state__4_1 (
    .in_2(board_controller__13_1_out_21), .out_4(out_17), .out_5(out_18), .out_6(out_19), .out_7(out_20),
    .out_8(out_21), .out_9(out_22), .out_10(out_23), .out_11(out_24), .out_12(out_25), .out_13(out_27),
    .out_14(out_29), .out_15(out_31), .out_16(out_33), .out_17(out_35), .out_18(out_39), .out_19(out_43),
    .out_20(out_46), .out_21(out_49), .out_22(out_26), .out_23(out_28), .out_24(out_30), .out_25(out_32),
    .out_26(out_34), .out_27(out_36), .out_28(out_40), .in_3(board_controller__13_1_out_23),
    .in_1(board_controller__13_1_out_24));
  GAME__SYSTEM__BASIC__14 game_system_basic__14_1 (
    .in_2(in_13), .in_3(in_14), .in_4(in_15), .in_5(in_16), .in_1(in_12), .out_6(out_69), .out_7(out_70));
endmodule

// #17
module UTILITY__DELAY__17 (
  input  in_1,
  input  [7:0] in_2,
  output out_3,
  output out_4
);

  wire and_1_out, clock_1_out;
  wire [7:0] counter_1_q;

  D_Flip_Flop d_ff_1 (.clk(in_1), .D(in_1), .Q(out_3), .reset(out_4));  // open: Qn, preset, en
  Clock clock_1 (.out(clock_1_out));
  and and_1 (and_1_out, out_3, clock_1_out);
  Counter counter_1 (.Q(counter_1_q), .clk(and_1_out), .clr(out_4));  // open: load, D, count, carry
  Comparator comparator_1 (.a(counter_1_q), .b(in_2), .eq(out_4));  // open: gt, lt
endmodule
